# Fritzing sketch 4WD-Rover (saved by Fritzing 1.0.6)

parts:
  DRV_1 = DRV 8825 Stepper Motor Carrier, High Current [part_number="DRV 8825"]
  DRV_3 = DRV 8825 Stepper Motor Carrier, High Current [part_number="DRV 8825"]
  DRV_4 = DRV 8825 Stepper Motor Carrier, High Current [part_number="DRV 8825"]
  SW1 = Slide_Switch_new
  DRV_2 = DRV 8825 Stepper Motor Carrier, High Current [part_number="DRV 8825"]
  C1 = Capacitor Polarized [package=cpol-radial-100uf-25v]
  C2 = Capacitor Polarized [package=cpol-radial-100uf-25v]
  C3 = Capacitor Polarized [package=cpol-radial-100uf-25v]
  C4 = Capacitor Polarized [package=cpol-radial-100uf-25v]
  D1 = Schottky Diode [part_number=1N5818 package="Melf DO-213 AB [SMD]"]
  M1 = Stepper Motor - Bipolar
  M2 = Stepper Motor - Bipolar
  M3 = Stepper Motor - Bipolar
  M4 = Stepper Motor - Bipolar
  VCC1 = Battery
  U1 = LuaNode32 / ESP32
  U2 = LM2596 step down module
  SEN1 = US-100 Ultrasonic Distance Sensor
  SEN2 = US-100 Ultrasonic Distance Sensor
  SEN3 = US-100 Ultrasonic Distance Sensor
  SEN4 = US-100 Ultrasonic Distance Sensor

nets:
  N1: DRV_1.ENABLE, DRV_3.ENABLE, DRV_4.ENABLE, DRV_2.ENABLE, U1.D4
  3.3V: DRV_1.MS3, DRV_1.RESET, DRV_1.SLEEP, DRV_3.MS3, DRV_3.RESET, DRV_3.SLEEP, DRV_4.MS3, DRV_4.RESET, DRV_4.SLEEP, DRV_2.MS3, DRV_2.RESET, DRV_2.SLEEP, U1.3V3, SEN1.VCC, SEN2.VCC, SEN3.VCC, SEN4.VCC
  N2: DRV_1.STEP, U1.D23
  N3: DRV_1.DIRECTION, U1.D22
  14.7V: DRV_1.VOLTAGE_ST/_MT, DRV_3.VOLTAGE_ST/_MT, DRV_4.VOLTAGE_ST/_MT, SW1.pin_1, DRV_2.VOLTAGE_ST/_MT, C1.+, C2.+, C3.+, C4.+, U2.IN+
  GND: DRV_1.GROUND_ST/_MT, DRV_3.GROUND_ST/_MT, DRV_4.GROUND_ST/_MT, DRV_2.GROUND_ST/_MT, C1.-, C2.-, C3.-, C4.-, VCC1.-, U1.GND, U2.IN-, U2.OUT-, SEN1.GND, SEN1.GND-2, SEN2.GND, SEN2.GND-2, SEN3.GND, SEN3.GND-2, SEN4.GND, SEN4.GND-2
  N4: DRV_1.OUT_2B, M1.A
  N5: DRV_1.OUT_2A, M1.C
  N6: DRV_1.OUT_1A, M1.B
  N7: DRV_1.OUT_1B, M1.D
  N8: DRV_3.STEP, U1.D18
  N9: DRV_3.DIRECTION, U1.D5
  N10: DRV_3.OUT_2B, M3.A
  N11: DRV_3.OUT_2A, M3.C
  N12: DRV_3.OUT_1A, M3.B
  N13: DRV_3.OUT_1B, M3.D
  N14: DRV_4.STEP, U1.D2
  N15: DRV_4.DIRECTION, U1.D15
  N16: DRV_4.OUT_2B, M4.A
  N17: DRV_4.OUT_2A, M4.C
  N18: DRV_4.OUT_1A, M4.B
  N19: DRV_4.OUT_1B, M4.D
  N20: SW1.pin_2, VCC1.+
  N21: DRV_2.STEP, U1.D21
  N22: DRV_2.DIRECTION, U1.D19
  N23: DRV_2.OUT_2B, M2.A
  N24: DRV_2.OUT_2A, M2.C
  N25: DRV_2.OUT_1A, M2.B
  N26: DRV_2.OUT_1B, M2.D
  N27: D1.cathode, U1.Vin
  5V: D1.anode, U2.OUT+
  N28: U1.D26, SEN1.ECHO
  N29: U1.D27, SEN2.ECHO
  N30: U1.D14, SEN3.ECHO
  N31: U1.D12, SEN1.TRIG, SEN2.TRIG, SEN3.TRIG, SEN4.TRIG
  N32: U1.D13, SEN4.ECHO

custom parts:
  Slide_Switch_new: the New two pin slide switch
  Battery: Your standard 2x 18650 battery pack (14.7 Volts)
  LuaNode32 / ESP32: ESP32 based LuaNode32
  LM2596 step down module: LM2596 DC-DC step down power supply module 3 A.
